// Logisim project Bit_Counter_DI.circ as structural Verilog: 1 circuit, main circuit main
module main (
  input  in_1,
  input  in_2,
  input  in_3,
  input  in_4,
  input  in_5,
  input  in_6,
  input  in_7,
  input  in_8
);

  wire and_1_out;

  and and_1 (and_1_out, in_1, in_3);
  // OR_Gate or_1 is placed but not wired
  LED led_1 ();  // open: in
  LED led_2 ();  // open: in
  LED led_3 (.in(and_1_out));
endmodule
